# Fritzing sketch smart-home (saved by Fritzing 0.9.3b)
breadboards: 1

parts:
  Raspberry_Pi_Pico_W = Raspberry Pi Pico W
  PIR_Sensor = HC-SR501 Body Sensor Module
  Passive_Buzzer = MH-FMD buzzer
  Keypad4x1 = Keypad Membran 4x4

nets:
  N1: Raspberry_Pi_Pico_W.pin_1, Keypad4x1.Pin5
  N2: Raspberry_Pi_Pico_W.pin_2, Keypad4x1.Pin6
  N3: Raspberry_Pi_Pico_W.pin_4, Keypad4x1.Pin7
  N4: Raspberry_Pi_Pico_W.pin_5, Keypad4x1.Pin8
  N5: Raspberry_Pi_Pico_W.pin_17, Passive_Buzzer.Pin_2
  N6: Raspberry_Pi_Pico_W.pin_18, Raspberry_Pi_Pico_W.pin_33, PIR_Sensor.GND, Passive_Buzzer.Pin_3
  N7: Raspberry_Pi_Pico_W.pin_27, Keypad4x1.Pin1
  N8: Raspberry_Pi_Pico_W.pin_29, Keypad4x1.Pin2
  N9: Raspberry_Pi_Pico_W.pin_31, Keypad4x1.Pin3
  N10: Raspberry_Pi_Pico_W.pin_32, Keypad4x1.Pin4
  N11: Raspberry_Pi_Pico_W.pin_34, PIR_Sensor.OUT
  N12: Raspberry_Pi_Pico_W.pin_40, PIR_Sensor.VCC, Passive_Buzzer.Pin_1

custom parts:
  Raspberry Pi Pico W: Raspberry Pi Pico W. Based around the RP2040 microcontroller the Pico W is a low cost microcontroller device bringing Raspberry Pi quality, cost, and easy of use to the microcontroller space. The areas marked KEEPOUT in pcb silkscreen should not have traces running through them to avoid shorts on a soldered in module!
  HC-SR501 Body Sensor Module: Pyroelectric Infrared PIR Motion Sensor Detector Module
  MH-FMD buzzer: MH-FMD buzzer.
  Keypad Membran 4x4: Membrane Keypad 4x4 Matrix
